# Fritzing sketch doors1 (saved by Fritzing 0.9.10b)
breadboards: 1

parts:
  Part1 = Arduino Uno (Rev3)
  S1 = SWITCH-MOMENTARY-2 [package=tactile_switch_tall]
  S2 = Momentary Switch [package=ksa_sealed_tac_switch]  # not connected
  S3 = SWITCH-MOMENTARY-2 [package=tactile_switch_tall]  # not connected
  R1 = Resistor [tolerance=±5% resistance=220 package="1206 [SMD]"]  # not connected

nets:
  N1: Part1.D2, Part1.5V, S1.1
  N2: Part1.GND, S1.2
